# Fritzing sketch 8x8 Dumb Brick (saved by Fritzing 0.9.2b)
breadboards: 1

parts:
  U2 = attiny85 [package=dip]
  Q1 = LTR-301 [package=ltr-301]
  LED1 = IR LED - 3mm [package="3 mm [THT]"]
  IC1 = Voltage Regulator [package=to-92]
  BAT1 = Battery Holders [package=battery-aa-panel]
  JP1 = Header 8 [package=bm08b-srss-tb]
  C1 = Ceramic Capacitor [capacitance=10nF package="100 mil [THT, multilayer]"]
  R1 = Resistor [tolerance=±5% resistance=4.7k package=THT]
  R2 = Resistor [tolerance=±5% resistance=4.7k package=THT]
  R3 = Resistor [tolerance=±5% resistance=4.7k package=THT]
  R4 = Resistor [tolerance=±5% resistance=68k package=THT]
  R5 = Resistor [tolerance=±5% resistance=10k package=THT]
  R6 = Resistor [tolerance=±5% resistance=330 package=THT]
  IC2 = IC, DIP package, 24 pins [chip_label=IC part_number=MAX7219]
  JP2 = Header 8 [package=bm08b-srss-tb]
  JP3 = Header 4 [package=screwterminal-3.5mm-4_lock]

nets:
  N1: U2.Pin_1, JP3.1
  N2: U2.Pin_2, R6.Pin_1
  N3: U2.Pin_3, Q1.C, R5.Pin_0
  GND: U2.Pin_4, Q1.E, LED1.cathode, IC1.GND, BAT1.+, C1.0, IC2.pin4, IC2.pin9
  N4: U2.Pin_5, R3.Pin_0, JP3.4
  N5: U2.Pin_6, R2.Pin_0, JP3.3
  N6: U2.Pin_7, R1.Pin_0, JP3.2
  5V: U2.Pin_8, IC1.OUT, R4.Pin_1, R5.Pin_1, IC2.pin19
  N7: LED1.anode, R6.Pin_0
  N8: IC1.IN, BAT1.-, C1.1
  N9: JP1.1, IC2.pin20
  N10: JP1.2, IC2.pin14
  N11: JP1.3, IC2.pin11
  N12: JP1.4, IC2.pin6
  N13: JP1.5, IC2.pin22
  N14: JP1.6, IC2.pin3
  N15: JP1.7, IC2.pin16
  N16: JP1.8, IC2.pin21
  N17: R1.Pin_1, IC2.pin13
  N18: R2.Pin_1, IC2.pin12
  N19: R3.Pin_1, IC2.pin1
  N20: R4.Pin_0, IC2.pin18
  N21: IC2.pin2, JP2.4
  N22: IC2.pin5, JP2.2
  N23: IC2.pin7, JP2.7
  N24: IC2.pin8, JP2.1
  N25: IC2.pin10, JP2.6
  N26: IC2.pin15, JP2.3
  N27: IC2.pin17, JP2.8
  N28: IC2.pin23, JP2.5

notes:
  RESET (orange)
  SCK (blue)
  MISO (yellow)
  MOSI (green)
  LED Matrix Block

custom parts:
  IR LED - 3mm: A generic IR LED (~1.8V)
